# Fritzing sketch RemoteControlledCar (saved by Fritzing 0.9.3b)

parts:
  Componente1 = Arduino Mega 2560 (Rev3)
  Componente2 = Bluetooth HC-05 Macho
  Componente3 = Arduino Motor Shield (Rev3)
  M4 = DC Motor
  BAT1 = BC9VPC [package=bc9vpc]
  M5 = DC Motor

nets:
  N1: Componente1.D19/RX1, Componente2.TXD
  N2: Componente1.D18/TX1, Componente2.RXD
  VCC: Componente2.VCC, Componente3.5V
  GND: Componente2.GND, Componente3.GND, BAT1.V-
  N3: Componente3.B-, M5.pin_2
  N4: Componente3.B+, M5.pin_1
  N5: Componente3.A-, M4.pin_2
  N6: Componente3.A+, M4.pin_1
  N7: Componente3.VMOT, BAT1.V+
